# Fritzing sketch Cthulu PI Controller Manual Route C (saved by Fritzing 0.9.3b)
circuit board: 15cm x 7.5cm
breadboards: 2

parts:
  U10 = 4011 4 x 2 Input NAND Gate, single part [part_number=4011 package="DIP (Dual Inline) [THT]"]
  U11 = 4011 4 x 2 Input NAND Gate, single part [part_number=4011 package="DIP (Dual Inline) [THT]"]
  U12 = 4011 4 x 2 Input NAND Gate, single part [part_number=4011 package="DIP (Dual Inline) [THT]"]
  J1 = Camdenboss CTB0158-6 [part_number=CTB0158-6 package=THT]
  J2 = Camdenboss CTB0158-4 [part_number=CTB0158-4 package=THT]
  IC3 = L293D [package=THT]
  IC4 = L293D [package=THT]
  J3 = Camdenboss CTB0158-4 [part_number=CTB0158-4 package=THT]
  J4 = Camdenboss CTB0158-4 [part_number=CTB0158-4 package=THT]
  R10 = Resistor [tolerance=±5% resistance=1k package="0805 [SMD]"]
  R11 = Resistor [tolerance=±5% resistance=220 package="0805 [SMD]"]
  Q3 = NPN-Transistor [package="TO92 [THT]"]
  LED3 = smd LED [color="Red (633nm)" package="1206 [SMD]"]
  R12 = Resistor [tolerance=±5% resistance=1k package="0805 [SMD]"]
  Q4 = NPN-Transistor [package="TO92 [THT]"]
  LED4 = smd LED [color="Red (633nm)" package="1206 [SMD]"]
  R13 = Resistor [tolerance=±5% resistance=220 package="0805 [SMD]"]
  R14 = Resistor [tolerance=±5% resistance=1k package="0805 [SMD]"]
  Q5 = NPN-Transistor [package="TO92 [THT]"]
  LED5 = smd LED [color="Red (633nm)" package="1206 [SMD]"]
  R15 = Resistor [tolerance=±5% resistance=220 package="0805 [SMD]"]
  R16 = Resistor [tolerance=±5% resistance=1k package="0805 [SMD]"]
  Q6 = NPN-Transistor [package="TO92 [THT]"]
  LED6 = smd LED [color="Red (633nm)" package="1206 [SMD]"]
  R17 = Resistor [tolerance=±5% resistance=220 package="0805 [SMD]"]

nets (from the pcb view):
  N1: U10.Q2, U10.A3, U10.B4
  N2: U10.A2, U10.B2, U12.A3, U12.A4, J1.pin1
  GND: U10.GND, U11.GND, U12.GND, J2.pin2, IC3.0V, IC4.0V, R11.Pin_1, R13.Pin_1, R15.Pin_1, R17.Pin_1
  N3: U10.B3, U12.B3, J1.pin2
  N4: U10.Q3, U11.A2, U11.B2
  N5: U10.Q4, U11.A1, U11.B1
  N6: U10.A4, U12.B4, J1.pin3
  VDD: U10.VDD, U11.VDD, U12.VDD, J2.pin1, IC3.+V, IC4.+V, Q3.C, Q4.C, Q5.C, Q6.C
  N7: U11.Q1, IC3.Enable_2, R12.Pin_1
  N8: U11.Q2, IC3.Enable_1, R10.Pin_1
  N9: U12.A1, U12.B1, U12.Q4
  N10: U12.Q1, IC4.Enable_2, R16.Pin_1
  N11: U12.Q2, IC4.Enable_1, R14.Pin_1
  N12: U12.A2, U12.B2, U12.Q3
  N13: J1.pin4, IC3.In_1, IC3.In_3, IC4.In_1, IC4.In_3
  N14: J1.pin5, IC4.In_4
  N15: J2.pin3, IC3.+Vmotor, IC4.+Vmotor
  N16: IC3.Out_1_(_Controlled_by_Enable_1_), J3.pin3
  N17: IC3.Out_2_(_Controlled_by_Enable_1_), J3.pin4
  N18: IC3.In_2, IC3.In_4, IC4.In_2
  N19: IC3.Out_3_(_Controlled_by_Enable_2_), J3.pin1
  N20: IC3.Out_4_(_Controlled_by_Enable_2_), J3.pin2
  N21: IC4.Out_1_(_Controlled_by_Enable_1_), J4.pin3
  N22: IC4.Out_2_(_Controlled_by_Enable_1_), J4.pin4
  N23: IC4.Out_3_(_Controlled_by_Enable_2_), J4.pin1
  N24: IC4.Out_4_(_Controlled_by_Enable_2_), J4.pin2
  N25: R10.Pin_0, Q3.B
  N26: R11.Pin_0, LED3.cathode
  N27: Q3.E, LED3.anode
  N28: R12.Pin_0, Q4.B
  N29: Q4.E, LED4.anode
  N30: LED4.cathode, R13.Pin_0
  N31: R14.Pin_0, Q5.B
  N32: Q5.E, LED5.anode
  N33: LED5.cathode, R15.Pin_0
  N34: R16.Pin_0, Q6.B
  N35: Q6.E, LED6.anode
  N36: LED6.cathode, R17.Pin_0
