# Fritzing sketch Cthulu PI Controller Manual Route D (saved by Fritzing 0.9.3b)
circuit board: 15cm x 7.5cm
breadboards: 3

parts:
  U11 = 4011 4 x 2 Input NAND Gate, single part [part_number=4011 package="DIP (Dual Inline) [THT]"]
  U12 = 4011 4 x 2 Input NAND Gate, single part [part_number=4011 package="DIP (Dual Inline) [THT]"]
  U13 = 4011 4 x 2 Input NAND Gate, single part [part_number=4011 package="DIP (Dual Inline) [THT]"]
  J3 = Camdenboss CTB0158-4 [part_number=CTB0158-4 package=THT]
  J4 = Camdenboss CTB0158-6 [part_number=CTB0158-6 package=THT]
  IC4 = L293D [package=THT]
  IC5 = L293D [package=THT]
  J5 = Camdenboss CTB0158-4 [part_number=CTB0158-4 package=THT]
  J6 = Camdenboss CTB0158-4 [part_number=CTB0158-4 package=THT]
  Q4 = NPN-Transistor [package="TO92 [THT]"]
  R12 = Resistor [tolerance=±5% resistance=1k package="0805 [SMD]"]
  R13 = Resistor [tolerance=±5% resistance=220 package="0805 [SMD]"]
  LED4 = smd LED [color="Red (633nm)" package="1206 [SMD]"]
  Q5 = NPN-Transistor [package="TO92 [THT]"]
  R14 = Resistor [tolerance=±5% resistance=1k package="0805 [SMD]"]
  R15 = Resistor [tolerance=±5% resistance=220 package="0805 [SMD]"]
  LED5 = smd LED [color="Red (633nm)" package="1206 [SMD]"]
  Q6 = NPN-Transistor [package="TO92 [THT]"]
  R16 = Resistor [tolerance=±5% resistance=1k package="0805 [SMD]"]
  R17 = Resistor [tolerance=±5% resistance=220 package="0805 [SMD]"]
  LED6 = smd LED [color="Red (633nm)" package="1206 [SMD]"]
  Q7 = NPN-Transistor [package="TO92 [THT]"]
  R18 = Resistor [tolerance=±5% resistance=1k package="0805 [SMD]"]
  R19 = Resistor [tolerance=±5% resistance=220 package="0805 [SMD]"]
  LED7 = smd LED [color="Red (633nm)" package="1206 [SMD]"]

nets (from the pcb view):
  N1: U11.Q2, U11.A3, U11.B4
  N2: U11.A2, U11.B2, U13.A3, U13.A4, J4.pin1
  GND: U11.GND, U12.GND, U13.GND, J3.pin2, IC4.0V, IC5.0V, R13.Pin_1, R15.Pin_1, R17.Pin_1, R19.Pin_1
  N3: U11.B3, U13.B3, J4.pin2
  N4: U11.Q3, U12.A2, U12.B2
  N5: U11.Q4, U12.A1, U12.B1
  N6: U11.A4, U13.B4, J4.pin3
  VDD: U11.VDD, U12.VDD, U13.VDD, J3.pin1, IC4.+V, IC5.+V, Q4.C, Q5.C, Q6.C, Q7.C
  N7: U12.Q1, IC4.Enable_2, R14.Pin_1
  N8: U12.Q2, IC4.Enable_1, R12.Pin_1
  N9: U13.A1, U13.B1, U13.Q4
  N10: U13.Q1, IC5.Enable_2, R18.Pin_1
  N11: U13.Q2, IC5.Enable_1, R16.Pin_1
  N12: U13.A2, U13.B2, U13.Q3
  N13: J3.pin3, IC4.+Vmotor, IC5.+Vmotor
  N14: J4.pin4, IC4.In_1, IC4.In_3, IC5.In_1, IC5.In_3
  N15: J4.pin5, IC5.In_2, IC5.In_4
  N16: IC4.Out_1_(_Controlled_by_Enable_1_), J5.pin1
  N17: IC4.Out_2_(_Controlled_by_Enable_1_), J5.pin2
  N18: IC4.In_2, IC4.In_4
  N19: IC4.Out_3_(_Controlled_by_Enable_2_), J5.pin3
  N20: IC4.Out_4_(_Controlled_by_Enable_2_), J5.pin4
  N21: IC5.Out_1_(_Controlled_by_Enable_1_), J6.pin1
  N22: IC5.Out_2_(_Controlled_by_Enable_1_), J6.pin2
  N23: IC5.Out_3_(_Controlled_by_Enable_2_), J6.pin3
  N24: IC5.Out_4_(_Controlled_by_Enable_2_), J6.pin4
  N25: Q4.E, LED4.anode
  N26: Q4.B, R12.Pin_0
  N27: R13.Pin_0, LED4.cathode
  N28: Q5.E, LED5.anode
  N29: Q5.B, R14.Pin_0
  N30: R15.Pin_0, LED5.cathode
  N31: Q6.E, LED6.anode
  N32: Q6.B, R16.Pin_0
  N33: R17.Pin_0, LED6.cathode
  N34: Q7.E, LED7.anode
  N35: Q7.B, R18.Pin_0
  N36: R19.Pin_0, LED7.cathode
