# Fritzing sketch Cthulu Pi Controller Manual Route E (saved by Fritzing 0.9.3b)
circuit board: 10cm x 10cm
breadboards: 1

parts:
  J4 = Camdenboss CTB0158-4 [part_number=CTB0158-4 package=THT]  # not connected
  J5 = Camdenboss CTB0158-4 [part_number=CTB0158-4 package=THT]  # not connected
  J6 = Camdenboss CTB0158-4 [part_number=CTB0158-4 package=THT]  # not connected
  J7 = Camdenboss CTB0158-6 [part_number=CTB0158-6 package=THT]  # not connected
  Q5 = NPN-Transistor [package="TO92 [THT]"]
  R14 = Resistor [tolerance=±5% resistance=1k package="0805 [SMD]"]
  R15 = Resistor [tolerance=±5% resistance=220 package="0805 [SMD]"]
  LED5 = smd LED [color="Red (633nm)" package="1206 [SMD]"]

nets:
  N1: Q5.E, LED5.anode
  N2: Q5.B, R14.Pin_0
  N3: R15.Pin_0, LED5.cathode
