# Fritzing sketch Cthulu Pi Controller Manual Route F (saved by Fritzing 0.9.3b)
circuit board: 14.9859cm x 8.28222cm
breadboards: 1

parts:
  R14 = Resistor [tolerance=±5% resistance=220 package="0805 [SMD]"]
  R15 = Resistor [tolerance=±5% resistance=220 package="0805 [SMD]"]
  R16 = Resistor [tolerance=±5% resistance=220 package="0805 [SMD]"]
  R17 = Resistor [tolerance=±5% resistance=220 package="0805 [SMD]"]
  LED8 = smd LED [color="Red (633nm)" package="1206 [SMD]"]
  LED9 = smd LED [color="Red (633nm)" package="1206 [SMD]"]
  LED10 = smd LED [color="Red (633nm)" package="1206 [SMD]"]
  LED11 = smd LED [color="Red (633nm)" package="1206 [SMD]"]
  Q6 = NPN-Transistor [package="TO92 [THT]"]
  Q7 = NPN-Transistor [package="TO92 [THT]"]
  Q8 = NPN-Transistor [package="TO92 [THT]"]
  Q9 = NPN-Transistor [package="TO92 [THT]"]
  R18 = Resistor [tolerance=±5% resistance=1k package="0805 [SMD]"]
  R19 = Resistor [tolerance=±5% resistance=1k package="0805 [SMD]"]
  R20 = Resistor [tolerance=±5% resistance=1k package="0805 [SMD]"]
  R21 = Resistor [tolerance=±5% resistance=1k package="0805 [SMD]"]
  J6 = Camdenboss CTB0158-4 [part_number=CTB0158-4 package=THT]
  J7 = Camdenboss CTB0158-4 [part_number=CTB0158-4 package=THT]
  J8 = Camdenboss CTB0158-4 [part_number=CTB0158-4 package=THT]
  J9 = Camdenboss CTB0158-6 [part_number=CTB0158-6 package=THT]
  U12 = 4011 4 x 2 Input NAND Gate, single part [part_number=4011 package="DIP (Dual Inline) [THT]"]
  U13 = 4011 4 x 2 Input NAND Gate, single part [part_number=4011 package="DIP (Dual Inline) [THT]"]
  U14 = 4011 4 x 2 Input NAND Gate, single part [part_number=4011 package="DIP (Dual Inline) [THT]"]
  IC5 = L293D [package=THT]
  IC6 = L293D [package=THT]

nets:
  N1: R14.Pin_0, LED8.cathode
  GND: R14.Pin_1, R15.Pin_1, R16.Pin_1, R17.Pin_1, J8.pin4, U12.GND, U13.GND, U14.GND, IC5.0V, IC6.0V
  N2: R15.Pin_0, LED9.cathode
  N3: R16.Pin_0, LED10.cathode
  N4: R17.Pin_0, LED11.cathode
  N5: LED8.anode, Q8.E
  N6: LED9.anode, Q7.E
  N7: LED10.anode, Q6.E
  N8: LED11.anode, Q9.E
  N9: Q6.B, R19.Pin_1
  VDD: Q6.C, Q7.C, Q8.C, Q9.C, J8.pin3, U12.VDD, U13.VDD, U14.VDD, IC5.+V, IC6.+V
  N10: Q7.B, R20.Pin_1
  N11: Q8.B, R21.Pin_1
  N12: Q9.B, R18.Pin_1
  N13: R18.Pin_0, U14.Q1, IC5.Enable_1
  N14: R19.Pin_0, U14.Q2, IC5.Enable_2
  N15: R20.Pin_0, U14.Q3, IC6.Enable_1
  N16: R21.Pin_0, U14.Q4, IC6.Enable_2
  N17: J6.pin1, IC5.Out_1_(_Controlled_by_Enable_1_)
  N18: J6.pin2, IC5.Out_2_(_Controlled_by_Enable_1_)
  N19: J6.pin3, IC5.Out_3_(_Controlled_by_Enable_2_)
  N20: J6.pin4, IC5.Out_4_(_Controlled_by_Enable_2_)
  N21: J7.pin1, IC6.Out_1_(_Controlled_by_Enable_1_)
  N22: J7.pin2, IC6.Out_2_(_Controlled_by_Enable_1_)
  N23: J7.pin3, IC6.Out_3_(_Controlled_by_Enable_2_)
  N24: J7.pin4, IC6.Out_4_(_Controlled_by_Enable_2_)
  N25: J8.pin2, IC5.+Vmotor, IC6.+Vmotor
  N26: J9.pin1, U12.A2, U12.B2, U13.B1, U13.A2
  N27: J9.pin2, U12.B3, U13.B2
  N28: J9.pin3, U12.A4, U13.A1
  N29: J9.pin4, IC5.In_1, IC5.In_3, IC6.In_1, IC6.In_3
  N30: J9.pin5, IC5.In_2, IC5.In_4, IC6.In_2, IC6.In_4
  N31: U12.Q2, U12.A3, U12.B4
  N32: U12.Q3, U14.A1, U14.B1
  N33: U12.Q4, U14.A2, U14.B2
  N34: U13.Q1, U14.A4, U14.B4
  N35: U13.Q2, U14.A3, U14.B3
