# Fritzing sketch CthuluPi_Controller Manual Route B (saved by Fritzing 0.9.3b)
circuit board: 14.7522cm x 7.88382cm
breadboards: 2

parts:
  U7 = 4011 4 x 2 Input NAND Gate, single part [part_number=4011 package="DIP (Dual Inline) [THT]"]
  U8 = 4011 4 x 2 Input NAND Gate, single part [part_number=4011 package="DIP (Dual Inline) [THT]"]
  U9 = 4011 4 x 2 Input NAND Gate, single part [part_number=4011 package="DIP (Dual Inline) [THT]"]
  J3 = Screw terminal - 2 pins [package=THT]
  JP2 = Header 6 [package=1x06_smd_straight_combo]
  IC4 = H-Bridge [package=THT]
  IC5 = H-Bridge [package=THT]
  J4 = Screw terminal - 2 pins [package=THT]
  JP3 = Header 6 [package=1x06_smd_straight_combo]
  JP4 = Header 6 [package=1x06_smd_straight_combo]
  R11 = Resistor [tolerance=±5% resistance=220 package="0805 [SMD]"]
  Q3 = NPN-Transistor [package="TO92 [THT]"]
  LED3 = smd LED [color="Red (633nm)" package="1206 [SMD]"]
  R12 = Resistor [tolerance=±5% resistance=1k package="0805 [SMD]"]
  Q4 = NPN-Transistor [package="TO92 [THT]"]
  R13 = Resistor [tolerance=±5% resistance=1k package="0805 [SMD]"]
  R14 = Resistor [tolerance=±5% resistance=220 package="0805 [SMD]"]
  LED4 = smd LED [color="Red (633nm)" package="1206 [SMD]"]
  Q5 = NPN-Transistor [package="TO92 [THT]"]
  R15 = Resistor [tolerance=±5% resistance=1k package="0805 [SMD]"]
  R16 = Resistor [tolerance=±5% resistance=220 package="0805 [SMD]"]
  LED5 = smd LED [color="Red (633nm)" package="1206 [SMD]"]
  Q6 = NPN-Transistor [package="TO92 [THT]"]
  R17 = Resistor [tolerance=±5% resistance=1k package="0805 [SMD]"]
  LED6 = smd LED [color="Red (633nm)" package="1206 [SMD]"]
  R18 = Resistor [tolerance=±5% resistance=220 package="0805 [SMD]"]

nets:
  GND: U7.GND, U8.GND, U9.GND, J3.pin2, R11.Pin_0, R14.Pin_0, R16.Pin_0, R18.Pin_0
  N1: U7.A3, U7.B3, U7.Q4
  N2: U7.Q3, IC4.3_4EN, R17.Pin_0
  N3: U7.A4, U9.B1, JP2.4
  N4: U7.B4, U8.B3, U9.A3, U9.B3, JP2.6
  VDD: U7.VDD, U8.VDD, U9.VDD, J3.pin1, IC4.VCC1, IC5.VCC1, Q3.C, Q4.C, Q5.C, Q6.C
  N5: U8.A1, U8.B1, U9.Q1
  N6: U8.Q1, IC5.3_4EN, R13.Pin_0
  N7: U8.Q2, IC4.1_2EN, R15.Pin_0
  N8: U8.A2, U8.B2, U8.Q3
  N9: U8.A3, U9.A4, JP2.5
  N10: U8.Q4, IC5.1_2EN, R12.Pin_0
  N11: U8.A4, U8.B4, U9.Q4
  N12: U9.A1, U9.Q3, U9.B4
  N13: JP2.2, IC4.1A, IC4.3A, IC5.1A, IC5.3A
  N14: JP2.3, IC4.2A, IC4.4A, IC5.2A, IC5.4A
  N15: IC4.1Y, JP4.5
  GND1: IC4.GND1, IC4.GND2, IC4.GND3, IC4.GND4, IC5.GND1, IC5.GND2, IC5.GND3, IC5.GND4, J4.pin2
  N16: IC4.2Y, JP4.6
  N17: IC4.VCC2, IC5.VCC2, J4.pin1
  N18: IC4.3Y, JP4.4
  N19: IC4.4Y, JP4.3
  N20: IC5.1Y, JP3.5
  N21: IC5.2Y, JP3.6
  N22: IC5.3Y, JP3.4
  N23: IC5.4Y, JP3.3
  N24: R11.Pin_1, LED3.cathode
  N25: Q3.E, LED3.anode
  N26: Q3.B, R12.Pin_1
  N27: Q4.E, LED4.anode
  N28: Q4.B, R13.Pin_1
  N29: R14.Pin_1, LED4.cathode
  N30: Q5.E, LED5.anode
  N31: Q5.B, R15.Pin_1
  N32: R16.Pin_1, LED5.cathode
  N33: Q6.E, LED6.anode
  N34: Q6.B, R17.Pin_1
  N35: LED6.cathode, R18.Pin_1
