# Fritzing sketch CthuluPi_Controller (saved by Fritzing 0.9.3b)
circuit board: 15cm x 7.72578cm
breadboards: 2

parts:
  U7 = 4011 4 x 2 Input NAND Gate, single part [part_number=4011 package="DIP (Dual Inline) [THT]"]
  U8 = 4011 4 x 2 Input NAND Gate, single part [part_number=4011 package="DIP (Dual Inline) [THT]"]
  U9 = 4011 4 x 2 Input NAND Gate, single part [part_number=4011 package="DIP (Dual Inline) [THT]"]
  J3 = Screw terminal - 2 pins [package=THT]
  IC4 = H-Bridge [package=THT]
  IC5 = H-Bridge [package=THT]
  J4 = Screw terminal - 2 pins [package=THT]
  J5 = Camdenboss CTB0158-6 [part_number=CTB0158-6 package=THT]
  J6 = Camdenboss CTB0158-4 [part_number=CTB0158-4 package=THT]
  J7 = Camdenboss CTB0158-4 [part_number=CTB0158-4 package=THT]

nets:
  GND: U7.GND, U8.GND, U9.GND, J3.pin2
  N1: U7.A3, U7.B3, U7.Q4
  N2: U7.Q3, IC4.3_4EN
  N3: U7.A4, U9.B1, J5.pin3
  N4: U7.B4, U8.B3, U9.A3, U9.B3, J5.pin5
  VDD: U7.VDD, U8.VDD, U9.VDD, J3.pin1, IC4.VCC1, IC5.VCC1
  N5: U8.A1, U8.B1, U9.Q1
  N6: U8.Q1, IC5.3_4EN
  N7: U8.Q2, IC4.1_2EN
  N8: U8.A2, U8.B2, U8.Q3
  N9: U8.A3, U9.A4, J5.pin4
  N10: U8.Q4, IC5.1_2EN
  N11: U8.A4, U8.B4, U9.Q4
  N12: U9.A1, U9.Q3, U9.B4
  N13: IC4.1A, IC4.3A, IC5.1A, IC5.3A, J5.pin1
  N14: IC4.1Y, J7.pin2
  GND1: IC4.GND1, IC4.GND2, IC4.GND3, IC4.GND4, IC5.GND1, IC5.GND2, IC5.GND3, IC5.GND4, J4.pin2
  N15: IC4.2Y, J7.pin1
  N16: IC4.2A, IC4.4A, IC5.2A, IC5.4A, J5.pin2
  N17: IC4.VCC2, IC5.VCC2, J4.pin1
  N18: IC4.3Y, J7.pin3
  N19: IC4.4Y, J7.pin4
  N20: IC5.1Y, J6.pin2
  N21: IC5.2Y, J6.pin1
  N22: IC5.3Y, J6.pin3
  N23: IC5.4Y, J6.pin4
