# Fritzing sketch CthuluPi_LEDs (saved by Fritzing 0.9.3b)
circuit board: 8.46667cm x 2.8cm
perfboards: 1

parts:
  J1 = Screw terminal - 2 pins [package=THT]
  R1 = Resistor [tolerance=±5% resistance=220 package="0402 [SMD]"]
  LED1 = smd LED [color="Red (633nm)" package="0603 [SMD]"]
  Q2 = NPN-Transistor [package="TO92 [THT]"]
  R2 = Resistor [tolerance=±5% resistance=1k package="0402 [SMD]"]
  R3 = Resistor [tolerance=±5% resistance=220 package="0402 [SMD]"]
  LED2 = smd LED [color="Red (633nm)" package="0603 [SMD]"]
  Q3 = NPN-Transistor [package="TO92 [THT]"]
  R4 = Resistor [tolerance=±5% resistance=1k package="0402 [SMD]"]
  R5 = Resistor [tolerance=±5% resistance=220 package="0402 [SMD]"]
  LED3 = smd LED [color="Red (633nm)" package="0603 [SMD]"]
  Q4 = NPN-Transistor [package="TO92 [THT]"]
  R6 = Resistor [tolerance=±5% resistance=1k package="0402 [SMD]"]
  R7 = Resistor [tolerance=±5% resistance=220 package="0402 [SMD]"]
  LED4 = smd LED [color="Red (633nm)" package="0603 [SMD]"]
  Q5 = NPN-Transistor [package="TO92 [THT]"]
  R8 = Resistor [tolerance=±5% resistance=1k package="0402 [SMD]"]
  JP1 = Header 6 [package=1x06_smd_straight_combo]

nets:
  N1: J1.pin1, Q2.C, Q3.C, Q4.C, Q5.C
  N2: J1.pin2, R1.Pin_0, R3.Pin_0, R5.Pin_0, R7.Pin_0
  N3: R1.Pin_1, LED1.anode
  N4: LED1.cathode, Q2.E
  N5: Q2.B, R2.Pin_1
  N6: R2.Pin_0, JP1.6
  N7: R3.Pin_1, LED2.anode
  N8: LED2.cathode, Q3.E
  N9: Q3.B, R4.Pin_1
  N10: R4.Pin_0, JP1.5
  N11: R5.Pin_1, LED3.anode
  N12: LED3.cathode, Q4.E
  N13: Q4.B, R6.Pin_1
  N14: R6.Pin_0, JP1.4
  N15: R7.Pin_1, LED4.anode
  N16: LED4.cathode, Q5.E
  N17: Q5.B, R8.Pin_1
  N18: R8.Pin_0, JP1.3
