# Fritzing sketch LED Solder 1 (saved by Fritzing 0.9.3b)
perfboards: 1

parts:
  R1 = Resistor [tolerance=±5% resistance=220 package="0805 [SMD]"]
  R3 = Resistor [tolerance=±5% resistance=220 package="0805 [SMD]"]
  R4 = Resistor [tolerance=±5% resistance=220 package="0805 [SMD]"]
  R5 = Resistor [tolerance=±5% resistance=220 package="0805 [SMD]"]
  R6 = Resistor [tolerance=±5% resistance=1k package="0805 [SMD]"]
  R7 = Resistor [tolerance=±5% resistance=1k package="0805 [SMD]"]
  R8 = Resistor [tolerance=±5% resistance=1k package="0805 [SMD]"]
  R9 = Resistor [tolerance=±5% resistance=1k package="0805 [SMD]"]
  Q1 = NPN-Transistor [package="TO92 [THT]"]
  Q2 = NPN-Transistor [package="TO92 [THT]"]
  Q3 = NPN-Transistor [package="TO92 [THT]"]
  Q4 = NPN-Transistor [package="TO92 [THT]"]
  LED1 = smd LED [color="Red (633nm)" package="1206 [SMD]"]
  LED2 = smd LED [color="Red (633nm)" package="1206 [SMD]"]  # not connected
  LED3 = smd LED [color="Red (633nm)" package="1206 [SMD]"]  # not connected
  LED4 = smd LED [color="Red (633nm)" package="1206 [SMD]"]  # not connected
  J1 = Screw terminal - 2 pins [package=THT]
  Header1 = 2 pin header [package=THT]
  Header2 = 2 pin header [package=THT]
  Header3 = 2 pin header [package=THT]
  Header4 = 2 pin header [package=THT]

nets:
  N1: R1.Pin_0, R3.Pin_0, R4.Pin_0, R5.Pin_1, Q1.C, Q4.C, J1.pin2
  N2: R1.Pin_1, LED1.anode
  N3: R6.Pin_0, Header3.pin_1#1
  N4: R6.Pin_1, Q1.B
  N5: R7.Pin_0, Header4.pin_1#1
  N6: R8.Pin_0, Header2.pin_1#1
  N7: R9.Pin_0, Header1.pin_1#1
  N8: Q1.E, LED1.cathode
  N9: Q2.C, Q3.C

custom parts:
  2 pin header: 2 pin male to male header
