# Fritzing sketch Motor Driver Solder 2 (saved by Fritzing 0.9.3b)
perfboards: 2

parts:
  IC2 = L293D [package=THT]
  M1 = RioRand LM2596
  J2 = Power Jack [package=power_jack_pth]
  R10 = Resistor [tolerance=±5% resistance=1k package="0805 [SMD]"]  # not connected
  R11 = Resistor [tolerance=±5% resistance=1k package="0805 [SMD]"]  # not connected
  R12 = Resistor [tolerance=±5% resistance=1k package="0805 [SMD]"]  # not connected
  R13 = Resistor [tolerance=±5% resistance=1k package="0805 [SMD]"]  # not connected
  R14 = Resistor [tolerance=±5% resistance=220 package="0805 [SMD]"]  # not connected
  R15 = Resistor [tolerance=±5% resistance=220 package="0805 [SMD]"]  # not connected
  R16 = Resistor [tolerance=±5% resistance=220 package="0805 [SMD]"]  # not connected
  R17 = Resistor [tolerance=±5% resistance=220 package="0805 [SMD]"]  # not connected
  Q5 = NPN-Transistor [package="TO92 [THT]"]  # not connected
  Q6 = NPN-Transistor [package="TO92 [THT]"]  # not connected
  Q7 = NPN-Transistor [package="TO92 [THT]"]  # not connected
  Q8 = NPN-Transistor [package="TO92 [THT]"]  # not connected
  LED5 = smd LED [color="Red (633nm)" package="1206 [SMD]"]  # not connected
  LED6 = smd LED [color="Red (633nm)" package="1206 [SMD]"]  # not connected
  LED7 = smd LED [color="Red (633nm)" package="1206 [SMD]"]  # not connected
  J3 = Screw terminal - 2 pins [package=THT]  # not connected
  LED8 = smd LED [color="Red (633nm)" package="1206 [SMD]"]  # not connected
  M6 = DC Motor  # not connected
  JP1 = Header 4 [package=1x04-smd]  # not connected

nets:
  N1: IC2.+Vmotor, M1.Pin_1
  N2: M1.Pin_2, J2.GND
