# Fritzing sketch Motor Driver Solder (saved by Fritzing 0.9.3b)
perfboards: 3

parts:
  J1 = Screw terminal - 2 pins [package=THT]  # not connected
  J2 = Screw terminal - 2 pins [package=THT]  # not connected
  J3 = Screw terminal - 2 pins [package=THT]  # not connected
  IC1 = L293D [package=THT]
  IC2 = L293D [package=THT]
  M1 = DC Motor
  M2 = DC Motor
  M3 = DC Motor
  M4 = DC Motor

nets:
  N1: IC1.Out_1_(_Controlled_by_Enable_1_), M1.pin_2
  N2: IC1.In_2, IC1.In_4
  N3: IC1.Out_3_(_Controlled_by_Enable_2_), M3.pin_2
  N4: IC1.Out_4_(_Controlled_by_Enable_2_), M3.pin_1
  N5: IC2.Out_1_(_Controlled_by_Enable_1_), M4.pin_2
  N6: IC2.Out_2_(_Controlled_by_Enable_1_), M4.pin_1
  N7: IC2.Out_3_(_Controlled_by_Enable_2_), M2.pin_2
