# Fritzing sketch Pump Controller PCB 1 (saved by Fritzing 0.9.3b)
circuit board: 8.46667cm x 5.64444cm
breadboards: 1

parts:
  Gates_1 = 4011 4 x 2 Input NAND Gate, single part [part_number=4011 package="DIP (Dual Inline) [THT]"]
  Gates_2 = 4011 4 x 2 Input NAND Gate, single part [part_number=4011 package="DIP (Dual Inline) [THT]"]
  Gates_3 = 4011 4 x 2 Input NAND Gate, single part [part_number=4011 package="DIP (Dual Inline) [THT]"]
  JP1 = Header 8 [package=1x08_smd_combined]

nets:
  N1: Gates_1.A1, Gates_1.B1, Gates_2.A1, JP1.3
  N2: Gates_1.Q1, Gates_1.A2, Gates_1.A3
  N3: Gates_1.Q2, Gates_1.A4, Gates_1.B4
  N4: Gates_1.B2, Gates_2.B1, Gates_2.B3, JP1.4
  GND: Gates_1.GND, Gates_2.GND, Gates_3.GND, JP1.2
  N5: Gates_1.B3, Gates_2.A3, JP1.5
  N6: Gates_1.Q3, Gates_2.A2, Gates_2.B2
  VDD: Gates_1.VDD, Gates_2.VDD, Gates_3.VDD, JP1.1
  N7: Gates_2.Q1, Gates_2.A4, Gates_2.B4
  N8: Gates_2.Q3, Gates_3.A2, Gates_3.B2
