# Fritzing sketch PumpController (saved by Fritzing 0.9.3b)
breadboards: 1

parts:
  U1 = 4011 4 x 2 Input NAND Gate, multi-part [part_number=4011 package="DIP (Dual Inline) [THT]"]
  U1_1 = 4011_4_x_2_input_NAND_gate_multipart_subpart2 [part_number=4011]  # not connected
  U1_2 = 4011_4_x_2_input_NAND_gate_multipart_subpart3 [part_number=4011]  # not connected
  U1_3 = 4011_4_x_2_input_NAND_gate_multipart_subpart4 [part_number=4011]  # not connected
  U1_4 = 4011_4_x_2_input_NAND_gate_multipart_subpart5 [part_number=4011]  # not connected
  IC1 = H-Bridge [package=THT]
  IC2 = H-Bridge [package=THT]
  Raspberry_Pi_B_rev1 = Raspberry Pi B rev1
  U2_4 = 4011_4_x_2_input_NAND_gate_multipart_subpart5 [part_number=4011]  # not connected
  U2_2 = 4011_4_x_2_input_NAND_gate_multipart_subpart3 [part_number=4011]  # not connected
  U2_1 = 4011_4_x_2_input_NAND_gate_multipart_subpart2 [part_number=4011]  # not connected
  part = 4011_4_x_2_input_NAND_gate_multipart_subpart1 [part_number=4011]  # not connected
  U2 = 4011 4 x 2 Input NAND Gate, multi-part [part_number=4011 package="DIP (Dual Inline) [THT]"]
  U3_4 = 4011_4_x_2_input_NAND_gate_multipart_subpart5 [part_number=4011]  # not connected
  U3_3 = 4011_4_x_2_input_NAND_gate_multipart_subpart4 [part_number=4011]  # not connected
  U3_2 = 4011_4_x_2_input_NAND_gate_multipart_subpart3 [part_number=4011]  # not connected
  U3_1 = 4011_4_x_2_input_NAND_gate_multipart_subpart2 [part_number=4011]  # not connected
  U3 = 4011 4 x 2 Input NAND Gate, multi-part [part_number=4011 package="DIP (Dual Inline) [THT]"]
  LED1 = LED - 5mm [color="Red (633nm)" package="5 mm [THT]"]
  LED2 = LED - 5mm [color="Red (633nm)" package="5 mm [THT]"]
  LED3 = LED - 5mm [color="Red (633nm)" package="5 mm [THT]"]
  LED4 = LED - 5mm [color="Red (633nm)" package="5 mm [THT]"]
  M1 = RioRand LM2596
  J1 = Power Jack [package=power_jack_combo]
  M2 = DC Motor
  M3 = DC Motor
  M4 = DC Motor
  M5 = DC Motor

nets:
  N1: U1.connector0, U1.connector1, Raspberry_Pi_B_rev1.GPIO_21, U3.connector0, U3.connector11
  N2: U1.connector2, U1.connector4, U2.connector0
  N3: U1.connector3, U1.connector7, U1.connector8
  N4: U1.connector5, Raspberry_Pi_B_rev1.GPIO_18, U3.connector1
  GND1: U1.connector6, IC1.GND1, IC1.GND2, IC1.GND3, IC1.GND4, IC2.GND1, IC2.GND2, IC2.GND3, IC2.GND4, Raspberry_Pi_B_rev1.GPIO_10, U2.connector6, U3.connector6, M1.Pin_4
  N5: U1.connector9, LED1.anode
  N6: U1.connector13, U2.connector13, U3.connector13, M1.Pin_3
  N7: IC1.1_2EN, LED1.cathode
  N8: IC1.1A, IC1.4A, IC2.1A, IC2.4A, Raspberry_Pi_B_rev1.GPIO_23
  N9: IC1.1Y, M3.pin_2
  N10: IC1.2Y, M3.pin_1
  N11: IC1.2A, IC1.3A, IC2.2A, IC2.3A, Raspberry_Pi_B_rev1.GPIO_22
  N12: IC1.VCC2, IC2.VCC2, M1.Pin_1, J1.PWR
  N13: IC1.3_4EN, LED2.cathode
  N14: IC1.3Y, M5.pin_2
  N15: IC1.4Y, M5.pin_1
  N16: IC2.1_2EN, LED3.cathode
  N17: IC2.1Y, M2.pin_2
  N18: IC2.2Y, M2.pin_1
  N19: IC2.3_4EN, LED4.cathode
  N20: IC2.3Y, M4.pin_2
  N21: IC2.4Y, M4.pin_1
  N22: Raspberry_Pi_B_rev1.GPIO_17, U2.connector1, U3.connector12
  N23: U2.connector2, U2.connector4, U2.connector5
  N24: U2.connector3, LED2.anode
  N25: U3.connector2, U3.connector4, U3.connector5
  N26: U3.connector3, LED3.anode
  N27: U3.connector7, U3.connector8, U3.connector10
  N28: U3.connector9, LED4.anode
  N29: M1.Pin_2, J1.GNDBREAK
