# Fritzing sketch PumpController2 (saved by Fritzing 0.9.3b)
breadboards: 1

parts:
  Raspberry_Pi_1 = Raspberry Pi 3 [part_number=RPI-3-V1.2]
  U1 = 4011 4 x 2 Input NAND Gate, single part [part_number=4011 package="DIP (Dual Inline) [THT]"]
  U2 = 4011 4 x 2 Input NAND Gate, single part [part_number=4011 package="DIP (Dual Inline) [THT]"]
  U3 = 4011 4 x 2 Input NAND Gate, single part [part_number=4011 package="DIP (Dual Inline) [THT]"]
  IC1 = H-Bridge [package=THT]
  IC2 = H-Bridge [package=THT]
  M1 = RioRand LM2596
  J1 = Power Jack [package=power_jack_slot]
  R1 = Resistor [tolerance=±5% resistance=220 package=THT]
  LED1 = smd LED [color="Red (633nm)" package="0603 [SMD]"]
  R2 = Resistor [tolerance=±5% resistance=220 package=THT]
  R3 = Resistor [tolerance=±5% resistance=220 package=THT]
  R4 = Resistor [tolerance=±5% resistance=220 package=THT]
  LED2 = smd LED [color="Red (633nm)" package="0603 [SMD]"]
  LED3 = smd LED [color="Red (633nm)" package="0603 [SMD]"]
  LED4 = smd LED [color="Red (633nm)" package="0603 [SMD]"]

nets:
  N1: Raspberry_Pi_1.GPIO17, IC1.1A, IC1.3A, IC2.1A, IC2.3A
  N2: Raspberry_Pi_1.GPIO27, IC1.2A, IC1.4A, IC2.2A, IC2.4A
  N3: Raspberry_Pi_1.GPIO22, U3.A4
  GND: Raspberry_Pi_1.GND, U1.GND, U2.GND, U3.GND, IC1.GND1, IC1.GND2, IC2.GND1, IC2.GND2
  N4: Raspberry_Pi_1.GPIO24, U2.B2, U3.A1, U3.B1
  N5: Raspberry_Pi_1.GPIO23, U2.A2, U3.B2
  N6: U1.A1, U1.B1, U2.Q2
  N7: U1.Q1, IC1.1_2EN, LED4.anode
  VDD: U1.VDD, U2.VDD, U3.VDD, IC1.VCC1, IC2.VCC1, M1.Pin_3, R1.Pin_1, R2.Pin_1, R3.Pin_1, R4.Pin_1
  N8: U2.A1, U2.B1, U3.Q2
  N9: U2.Q1, IC2.1_2EN, LED3.anode
  N10: U2.Q4, IC1.3_4EN, LED1.anode
  N11: U2.A4, U3.A3, U3.B3, U3.Q4
  N12: U2.B4, U3.Q1, U3.A2, U3.B4
  N13: U3.Q3, IC2.3_4EN, LED2.anode
  N14: IC1.VCC2, IC2.VCC2, M1.Pin_1, J1.PWR
  GND3: IC1.GND3, IC1.GND4, IC2.GND3, IC2.GND4, M1.Pin_4
  N15: M1.Pin_2, J1.GND
  N16: R1.Pin_0, LED1.cathode
  N17: R2.Pin_0, LED2.cathode
  N18: R3.Pin_0, LED3.cathode
  N19: R4.Pin_0, LED4.cathode
