# Fritzing sketch PumpController3 (saved by Fritzing 0.9.3b)
circuit board: 8.46667cm x 5.64444cm
circuit board: 8.46667cm x 5.64444cm
breadboards: 2

parts:
  LED1 = LED - 3mm [color="Red (633nm)" package="3 mm [THT]"]
  Q1 = NPN-Transistor [package="SOT-23 [SMD]"]
  R1 = Resistor [tolerance=±5% resistance=220 package="0603 [SMD]"]
  R2 = Resistor [tolerance=±5% resistance=1k package="0603 [SMD]"]
  LED2 = LED - 3mm [color="Red (633nm)" package="3 mm [THT]"]
  Q2 = NPN-Transistor [package="SOT-23 [SMD]"]
  R3 = Resistor [tolerance=±5% resistance=1k package="0603 [SMD]"]
  Q3 = NPN-Transistor [package="SOT-23 [SMD]"]
  Q4 = NPN-Transistor [package="SOT-23 [SMD]"]
  R4 = Resistor [tolerance=±5% resistance=1k package="0603 [SMD]"]
  R5 = Resistor [tolerance=±5% resistance=1k package="0603 [SMD]"]
  LED3 = LED - 3mm [color="Red (633nm)" package="3 mm [THT]"]
  LED4 = LED - 3mm [color="Red (633nm)" package="3 mm [THT]"]
  R6 = Resistor [tolerance=±5% resistance=220 package="0603 [SMD]"]
  R7 = Resistor [tolerance=±5% resistance=220 package="0603 [SMD]"]
  R8 = Resistor [tolerance=±5% resistance=220 package="0603 [SMD]"]
  U1 = 4011 4 x 2 Input NAND Gate, single part [part_number=4011 package="DIP (Dual Inline) [THT]"]
  U2 = 4011 4 x 2 Input NAND Gate, single part [part_number=4011 package="DIP (Dual Inline) [THT]"]
  U3 = 4011 4 x 2 Input NAND Gate, single part [part_number=4011 package="DIP (Dual Inline) [THT]"]
  Raspberry_Pi_B_rev1 = Raspberry Pi B rev1
  IC3 = H-Bridge [package=THT]
  IC4 = H-Bridge [package=THT]
  M1 = DC Motor
  M2 = DC Motor
  M3 = DC Motor
  M4 = DC Motor
  M5 = RioRand LM2596
  J1 = Power Jack [package=power_jack_pth]

nets:
  N1: LED1.cathode, Q1.1
  N2: LED1.anode, R6.Pin_0
  VDD: Q1.2, Q2.2, Q3.2, Q4.2, U1.VDD, U2.VDD, U3.VDD, IC3.VCC1, IC4.VCC1, M5.Pin_3
  N3: Q1.0, R2.Pin_1
  N4: R1.Pin_0, LED2.anode
  GND: R1.Pin_1, R6.Pin_1, R8.Pin_1, U1.GND, U2.GND, U3.GND, IC3.GND1, IC3.GND2, IC3.GND3, IC3.GND4, IC4.GND1, IC4.GND2, IC4.GND3, IC4.GND4, M5.Pin_4
  N5: R2.Pin_0, U3.Q2, IC4.1_2EN
  N6: LED2.cathode, Q2.1
  N7: Q2.0, R3.Pin_1
  N8: R3.Pin_0, U3.Q3, IC4.3_4EN
  N9: Q3.0, R4.Pin_1
  N10: Q3.1, LED3.cathode
  N11: Q4.0, R5.Pin_1
  N12: Q4.1, LED4.cathode
  N13: R4.Pin_0, U2.Q2, IC3.3_4EN
  N14: R5.Pin_0, U2.Q3, IC3.1_2EN
  N15: LED3.anode, R7.Pin_0
  N16: LED4.anode, R8.Pin_0
  N17: U1.A1, U1.B1, U1.Q2
  N18: U1.Q1, U2.A2, U2.B2
  N19: U1.A2, U2.B1, Raspberry_Pi_B_rev1.GPIO_21
  N20: U1.B2, U1.Q3, U1.A4
  N21: U1.A3, U1.B3, U2.A1, U2.B4, Raspberry_Pi_B_rev1.GPIO_17
  N22: U1.Q4, U2.A3, U2.B3
  N23: U1.B4, U2.A4, Raspberry_Pi_B_rev1.GPIO_18
  N24: U2.Q1, U3.A2, U3.B2
  N25: U2.Q4, U3.A3, U3.B3
  N26: Raspberry_Pi_B_rev1.GPIO_23, IC3.1A, IC3.4A, IC4.1A, IC4.4A
  N27: Raspberry_Pi_B_rev1.GPIO_22, IC3.2A, IC3.3A, IC4.2A, IC4.3A
  N28: IC3.1Y, M1.pin_1
  N29: IC3.2Y, M1.pin_2
  N30: IC3.VCC2, IC4.VCC2, M5.Pin_2, J1.PWR
  N31: IC3.3Y, M2.pin_2
  N32: IC3.4Y, M2.pin_1
  N33: IC4.1Y, M3.pin_2
  N34: IC4.2Y, M3.pin_1
  N35: IC4.4Y, M4.pin_2
  N36: M5.Pin_1, J1.GNDBREAK
