# Fritzing sketch PumpController_Solder (saved by Fritzing 0.9.3b)
perfboards: 3

parts:
  M1 = RioRand LM2596
  J1 = Power Jack [package=power_jack_pth]
  J2 = Screw terminal - 2 pins [package=THT]
  J3 = Screw terminal - 2 pins [package=THT]
  U1 = 4011 4 x 2 Input NAND Gate, multi-part [part_number=4011 package="DIP (Dual Inline) [THT]"]  # not connected
  U2 = 4011 4 x 2 Input NAND Gate, multi-part [part_number=4011 package="DIP (Dual Inline) [THT]"]  # not connected
  U3 = 4011 4 x 2 Input NAND Gate, multi-part [part_number=4011 package="DIP (Dual Inline) [THT]"]  # not connected
  Raspberry_Pi_B_rev1 = Raspberry Pi B rev1  # not connected
  IC1 = L293D [package=THT]  # not connected
  IC2 = L293D [package=THT]  # not connected

nets:
  N1: M1.Pin_2, J1.GND
  N2: M1.Pin_3, J3.pin2
  N3: M1.Pin_4, J3.pin1
  N4: J1.PWR, J2.pin2

notes:
  12V Power Rail
